// Logisim project BCD ADDAR.circ as structural Verilog: 1 circuit, main circuit main
module main (
  input  B3,
  input  B2,
  input  B1,
  input  B0,
  input  A3,
  input  A2,
  input  A1,
  input  A0,
  input  [3:0] B,
  input  [3:0] A,
  input  Cin,
  input  Cin_2,
  output [3:0] SUM,
  output C_out,
  output S3,
  output S2,
  output S1,
  output S0
);

  wire adder_1_cout, adder_1_out, adder_3_cout, adder_3_out, adder_4_cout, adder_5_cout, adder_5_out,
       adder_6_cout, adder_7_cout, adder_7_out, adder_8_cout, and_1_out, and_2_out, or_1_out;

  or or_1 (or_1_out, adder_1_cout, and_1_out, and_2_out);
  and and_1 (and_1_out, adder_1_out, adder_3_out);
  and and_2 (and_2_out, adder_1_out, adder_5_out);
  Adder #(.width(1)) adder_1 (.a(A3), .b(B3), .out(adder_1_out), .cin(adder_3_cout), .cout(adder_1_cout));
  Adder #(.width(1)) adder_2 (.a(adder_1_out), .b(1'b0), .out(S3), .cin(adder_4_cout), .cout(C_out));
  Adder #(.width(1)) adder_3 (.a(A2), .b(B2), .out(adder_3_out), .cin(adder_5_cout), .cout(adder_3_cout));
  Adder #(.width(1)) adder_4 (.a(adder_3_out), .b(or_1_out), .out(S2), .cin(adder_6_cout), .cout(adder_4_cout));
  Adder #(.width(1)) adder_5 (.a(A1), .b(B1), .out(adder_5_out), .cin(adder_7_cout), .cout(adder_5_cout));
  Adder #(.width(1)) adder_6 (.a(adder_5_out), .b(or_1_out), .out(S1), .cin(adder_8_cout), .cout(adder_6_cout));
  Adder #(.width(1)) adder_7 (.a(A0), .b(B0), .out(adder_7_out), .cin(Cin_2), .cout(adder_7_cout));
  Adder #(.width(1)) adder_8 (.a(adder_7_out), .b(1'b0), .out(S0), .cout(adder_8_cout));  // open: cin
  Adder #(.width(4)) adder_9 (.a(A), .b(B), .out(SUM), .cin(Cin));  // open: cout

  // Notes on the sheet:
  //   GND
  //   S3
  //   S2
  //   S1
  //   S0
endmodule
