// Logisim project JK FLIP FLOP.circ as structural Verilog: 1 circuit, main circuit main
module main (
  input  in_1,
  output out_2,
  output q1,
  output q0
);

  wire and_1_out, clock_1_out, not_1_out, or_1_out, or_2_out;

  Clock clock_1 (.out(clock_1_out));
  not not_1 (not_1_out, in_1);
  and and_1 (and_1_out, q0, not_1_out);
  or or_1 (or_1_out, q0, in_1);
  or or_2 (or_2_out, q1, in_1);
  J_K_Flip_Flop j_k_ff_1 (.J(and_1_out), .clk(clock_1_out), .K(or_1_out), .Q(q1));  // open: Qn, preset, en, reset
  J_K_Flip_Flop j_k_ff_2 (.J(or_2_out), .clk(clock_1_out), .K(not_1_out), .Q(q0));  // open: Qn, preset, en, reset
  and and_2 (out_2, q1, in_1, q0);
endmodule
